// Logisim project cs20project1.circ as structural Verilog: 1 circuit, main circuit main
module main (
);

  wire Display_p3, Display_p5, Input_X_p1, Input_X_p2, Input_X_p3, Input_Y_p1, Input_Y_p2, Input_Y_p3,
       Input_Y_p4, Input_Y_p5, n7404_1_p4, n7404_1_p10, n7404_1_p14, n7408_1_p2, n7408_1_p4, n7408_1_p9,
       n7408_1_p11, n7408_2_p4, n7408_2_p6, n7408_2_p7, n7408_2_p8, n7408_2_p16, n7408_2_p17, n7408_3_p2,
       n7408_4_p2, n7408_4_p3, n7408_4_p9, n7408_4_p10, n7408_5_p3, n7408_5_p9, n7408_5_p10, n7408_6_p2,
       n7408_6_p4, n7408_6_p7, n7408_6_p12, n7421_1_p3, n7432_1_p2, n7432_1_p4, n7432_1_p6, n7432_1_p7,
       n7432_1_p8, n7432_1_p10, n7432_1_p12, n7432_1_p14, n7432_1_p15, n7432_2_p2, n7432_2_p3, n7432_2_p7,
       n7432_2_p9, n7432_2_p12, n7432_2_p13, n7432_2_p14, n7432_2_p15, n7432_3_p2, n7432_3_p10, n7432_3_p13,
       n7432_3_p15, n7432_4_p4, n7432_4_p10, n7483_1_p3;

  // DipSwitch Input_X: pin names not known; wires that end beside it: Input_X_p1, Input_X_p2, Input_X_p3
  // DipSwitch Input_Y: pin names not known; wires that end beside it: Input_Y_p1, Input_Y_p2, Input_Y_p3, Input_Y_p4, Input_Y_p5
  // _7432 7432_1: pin names not known; wires that end beside it: 1'b0, n7432_1_p2, n7432_1_p2, n7432_1_p4, n7432_1_p4, n7432_1_p6, n7432_1_p7, n7432_1_p8, n7432_1_p6, n7432_1_p10, n7432_1_p10, n7432_1_p12, n7432_1_p7, n7432_1_p14, n7432_1_p15, n7432_1_p4, 1'b1
  // DipSwitch Display: pin names not known; wires that end beside it: Input_Y_p1, Input_Y_p4, Display_p3, Input_X_p3, Display_p5
  // _7483 7483_1: pin names not known; wires that end beside it: Input_Y_p2, Input_X_p1, n7483_1_p3, n7432_1_p14, Input_X_p2, 1'b0, Input_Y_p3, 1'b0, 1'b1, Input_Y_p5, n7432_1_p7
  // _7408 7408_1: pin names not known; wires that end beside it: 1'b0, n7408_1_p2, n7408_1_p2, n7408_1_p4, n7432_1_p7, n7432_1_p12, n7432_1_p2, n7483_1_p3, n7408_1_p9, n7408_1_p9, n7408_1_p11, n7408_1_p11, n7432_1_p2, n7432_1_p10, n7432_1_p4, Display_p3, 1'b1
  // _7404 7404_1: pin names not known; wires that end beside it: 1'b1, n7432_1_p14, Display_p5, n7404_1_p4, n7404_1_p4, n7432_1_p6, n7432_1_p6, n7432_1_p7, n7483_1_p3, n7404_1_p10, n7404_1_p10, n7432_1_p8, Display_p3, n7404_1_p14, 1'b0
  // _7432 7432_2: pin names not known; wires that end beside it: 1'b0, n7432_2_p2, n7432_2_p3, n7432_2_p3, n7432_2_p3, n7408_1_p11, n7432_2_p7, n7408_1_p2, n7432_2_p9, n7432_2_p7, n7432_2_p7, n7432_2_p12, n7432_2_p13, n7432_2_p14, n7432_2_p15, 1'b1
  // _7408 7408_2: pin names not known; wires that end beside it: 1'b0, n7432_2_p14, n7432_2_p14, n7408_2_p4, n7408_2_p4, n7408_2_p6, n7408_2_p7, n7408_2_p8, n7432_1_p8, n7432_2_p12, n7432_2_p12, n7408_2_p6, n7408_2_p6, Display_p5, n7404_1_p10, n7408_2_p16, n7408_2_p17, 1'b1
  // _7408 7408_3: pin names not known; wires that end beside it: 1'b0, n7408_3_p2, n7432_1_p15, n7432_1_p15, n7432_1_p6, n7432_1_p8, n7432_1_p14, Display_p5, n7432_2_p15, n7408_2_p17, n7408_2_p17, Display_p5, n7483_1_p3, n7432_1_p14, Display_p5, 1'b1
  LED m1 (.in(n7408_1_p4));
  LED m2 (.in(1'b0));
  LED m3 (.in(1'b0));
  // _7408 7408_4: pin names not known; wires that end beside it: 1'b0, n7408_4_p2, n7408_4_p3, n7408_4_p3, Display_p5, n7404_1_p10, n7404_1_p14, n7483_1_p3, n7408_4_p9, n7408_4_p10, n7408_4_p10, n7404_1_p4, n7404_1_p10, n7404_1_p14, n7404_1_p4, 1'b1
  // _7432 7432_3: pin names not known; wires that end beside it: 1'b0, n7432_3_p2, n7432_3_p2, n7408_2_p16, n7408_2_p16, n7408_1_p9, n7408_2_p4, n7408_4_p3, n7408_4_p9, n7432_3_p10, n7408_2_p8, n7408_2_p8, n7432_3_p13, n7404_1_p14, n7432_3_p15, n7404_1_p4, 1'b1
  LED m4 (.in(n7408_3_p2));
  LED m5 (.in(1'b0));
  LED m6 (.in(1'b0));
  LED l1 (.in(n7432_2_p2));
  LED l4 (.in(n7432_3_p10));
  LED l2 (.in(n7432_2_p9));
  LED l5 (.in(n7432_4_p10));
  LED l6 (.in(1'b0));
  LED l3 (.in(1'b0));
  // _7408 7408_5: pin names not known; wires that end beside it: 1'b0, n7408_2_p7, n7408_5_p3, n7408_5_p3, n7432_1_p14, n7404_1_p10, n7432_1_p7, n7432_1_p8, n7408_5_p9, n7408_5_p10, n7408_5_p10, n7483_1_p3, n7432_1_p14, n7432_1_p7, n7432_1_p8, 1'b1
  // _7408 7408_6: pin names not known; wires that end beside it: 1'b0, n7408_6_p2, n7408_6_p2, n7408_6_p4, n7408_6_p4, n7408_4_p2, n7408_6_p7, n7408_4_p10, n7408_4_p2, n7432_3_p15, n7432_3_p15, n7408_6_p12, n7408_6_p12, n7432_2_p15, n7432_3_p2, n7432_1_p7, Display_p3, 1'b1
  // _7421 7421_1: pin names not known; wires that end beside it: 1'b0, n7432_2_p13, n7421_1_p3, n7421_1_p3, Display_p5, Display_p3, n7483_1_p3, n7432_1_p14, n7404_1_p10, n7432_1_p8, n7404_1_p14, Display_p5, 1'b1
  // _7432 7432_4: pin names not known; wires that end beside it: 1'b0, n7432_3_p13, n7432_3_p13, n7432_4_p4, n7432_4_p4, n7408_6_p12, n7408_6_p4, n7408_6_p4, n7421_1_p3, n7432_4_p10, n7408_6_p7, n7408_6_p7, n7408_6_p2, n7408_5_p9, n7432_4_p4, n7408_5_p3, 1'b1

  // Notes on the sheet:
  //   X3 X2 X1
  //   A'+D
  //   A'+B'
  //   A'+D$+C
  //   D+AB'
  //   Y3 Y2 Y1
  //   M1
  //   D(A'$+B')
  //   E(D+$AB')
  //   A'+B'D
  //   (Display) - A$(S4) - B$(S3) - C$(S2) - D$(S1) - E
  //   L1
  //   L2
  //   A'
  //   C'
  //   M4
  //   B'
  //   E'
  //   D'
  //   ABD'
  //   B'CD
  //   ABD'$(C'+E')
  //   AB
  //   AB'
  //   AC
  //   A'C
  //   A(C'E'$+B'CD)
  //   BD'
  //   C'E'+$B'CD
  //   A'+B'D$+BD'
  //   MSB
  //   TENS
  //   C'D'
  //   AE'
  //   C'E'
  //   C'+E'
  //   L4
  //   0-BINARY
  //   1-BRAILLE BCD
  //   B'D'
  //   CD
  //   AE'(B'D$+BD)
  //   AC'D'E'
  //   LSB
  //   ONES
  //   B'C
  //   BD
  //   E(A'+$B'D+BD')
  //   ACD
  //   AB'CE
  //   ABD'E'
  //   B'D+BD
  //   L5
endmodule
