// Logisim project cs20project2.circ as structural Verilog: 3 circuits, main circuit main
module main (
  input  A1,
  input  A0
);

  wire clock_1_out, mode_0_1_sub_circuit_1_d0, mode_0_1_sub_circuit_1_d1, mode_0_1_sub_circuit_1_d2,
       mode_0_1_sub_circuit_1_d3, mode_2_3_sub_circuit_1_d0, mode_2_3_sub_circuit_1_d1,
       mode_2_3_sub_circuit_1_d2, mode_2_3_sub_circuit_1_d3, mode_2_3_sub_circuit_1_d4, not_1_out, Q0_2_q,
       Q0_q, Q1_2_q, Q1_q, Q2_2_q, Q2_q, Q3_2_q, Q3_q, Q4_q;
  wire [6:0] mode_0_1_sub_circuit_1_a7, mode_2_3_sub_circuit_1_a7, multiplexer_1_out;

  Clock clock_1 (.out(clock_1_out));
  not not_1 (not_1_out, A1);
  mode_0_1_sub_circuit mode_0_1_sub_circuit_1 (
    .A0(A0), .Q3(Q3_q), .Q2(Q2_q), .Q1(Q1_q), .Q0(Q0_q), .D3(mode_0_1_sub_circuit_1_d3),
    .D2(mode_0_1_sub_circuit_1_d2), .D1(mode_0_1_sub_circuit_1_d1), .D0(mode_0_1_sub_circuit_1_d0),
    .A7(mode_0_1_sub_circuit_1_a7[0]), .B7(mode_0_1_sub_circuit_1_a7[1]), .C7(mode_0_1_sub_circuit_1_a7[2]),
    .D7(mode_0_1_sub_circuit_1_a7[3]), .E7(mode_0_1_sub_circuit_1_a7[4]), .F7(mode_0_1_sub_circuit_1_a7[5]),
    .G7(mode_0_1_sub_circuit_1_a7[6]));
  mode_2_3_sub_circuit mode_2_3_sub_circuit_1 (
    .A0(A0), .Q4(Q4_q), .Q3(Q3_2_q), .Q2(Q2_2_q), .Q1(Q1_2_q), .Q0(Q0_2_q), .D4(mode_2_3_sub_circuit_1_d4),
    .D3(mode_2_3_sub_circuit_1_d3), .D2(mode_2_3_sub_circuit_1_d2), .D1(mode_2_3_sub_circuit_1_d1),
    .D0(mode_2_3_sub_circuit_1_d0), .A7(mode_2_3_sub_circuit_1_a7[0]), .B7(mode_2_3_sub_circuit_1_a7[1]),
    .C7(mode_2_3_sub_circuit_1_a7[2]), .D7(mode_2_3_sub_circuit_1_a7[3]), .E7(mode_2_3_sub_circuit_1_a7[4]),
    .F7(mode_2_3_sub_circuit_1_a7[5]), .G7(mode_2_3_sub_circuit_1_a7[6]));
  D_Flip_Flop Q0 (.clk(clock_1_out), .D(mode_0_1_sub_circuit_1_d0), .Q(Q0_q), .reset(A1));  // open: Qn, preset, en
  D_Flip_Flop Q0_2 (
    .clk(clock_1_out), .D(mode_2_3_sub_circuit_1_d0), .Q(Q0_2_q), .reset(not_1_out));  // open: Qn, preset, en
  D_Flip_Flop Q1 (.clk(clock_1_out), .D(mode_0_1_sub_circuit_1_d1), .Q(Q1_q), .reset(A1));  // open: Qn, preset, en
  Multiplexer #(.width(7)) multiplexer_1 (
    .in0(mode_0_1_sub_circuit_1_a7), .in1(mode_2_3_sub_circuit_1_a7), .out(multiplexer_1_out), .sel(A1));  // open: en
  D_Flip_Flop Q2 (.clk(clock_1_out), .D(mode_0_1_sub_circuit_1_d2), .Q(Q2_q), .reset(A1));  // open: Qn, preset, en
  D_Flip_Flop Q1_2 (
    .clk(clock_1_out), .D(mode_2_3_sub_circuit_1_d1), .Q(Q1_2_q), .reset(not_1_out));  // open: Qn, preset, en
  D_Flip_Flop Q3 (.clk(clock_1_out), .D(mode_0_1_sub_circuit_1_d3), .Q(Q3_q), .reset(A1));  // open: Qn, preset, en
  _7_Segment_Display u_7_segment_display_1 (
    .g(multiplexer_1_out[6]), .f(multiplexer_1_out[5]), .a(multiplexer_1_out[0]), .b(multiplexer_1_out[1]),
    .e(multiplexer_1_out[4]), .d(multiplexer_1_out[3]), .c(multiplexer_1_out[2]));  // open: dp
  D_Flip_Flop Q2_2 (
    .clk(clock_1_out), .D(mode_2_3_sub_circuit_1_d2), .Q(Q2_2_q), .reset(not_1_out));  // open: Qn, preset, en
  D_Flip_Flop Q3_2 (
    .clk(clock_1_out), .D(mode_2_3_sub_circuit_1_d3), .Q(Q3_2_q), .reset(not_1_out));  // open: Qn, preset, en
  D_Flip_Flop Q4 (
    .clk(clock_1_out), .D(mode_2_3_sub_circuit_1_d4), .Q(Q4_q), .reset(not_1_out));  // open: Qn, preset, en

  // Notes on the sheet:
  //   Mode 0 / Mode 1
  //   Mode 2 / Mode 3
endmodule

module mode_0_1_sub_circuit (
  input  A0,
  input  Q3,
  input  Q2,
  input  Q1,
  input  Q0,
  output D3,
  output D2,
  output D1,
  output D0,
  output A7,
  output B7,
  output C7,
  output D7,
  output E7,
  output F7,
  output G7
);

  wire and_1_out, and_2_out, and_3_out, and_4_out, and_5_out, and_6_out, and_7_out, and_8_out, and_9_out,
       and_10_out, and_11_out, and_12_out, and_13_out, and_14_out, and_15_out, and_16_out, and_17_out,
       and_18_out, and_19_out, and_20_out, and_21_out, and_22_out, and_23_out, and_24_out, and_25_out,
       and_26_out, and_27_out, and_28_out, and_29_out, and_30_out, and_31_out, and_32_out, and_33_out,
       and_34_out, and_35_out, and_36_out, and_37_out, and_38_out, and_39_out, and_40_out, and_41_out,
       and_42_out, and_43_out, not_1_out, not_2_out, not_3_out, not_4_out, not_5_out;

  not not_1 (not_1_out, A0);
  not not_2 (not_2_out, Q3);
  not not_3 (not_3_out, Q2);
  not not_4 (not_4_out, Q1);
  not not_5 (not_5_out, Q0);
  and and_1 (and_1_out, A0, not_2_out, not_3_out, not_4_out, Q0);
  and and_2 (and_2_out, A0, not_2_out, not_3_out, Q1, not_5_out);
  or or_1 (D3, and_1_out, and_2_out, and_3_out, and_4_out);
  and and_3 (and_3_out, A0, not_2_out, Q2, Q1, Q0);
  and and_4 (and_4_out, A0, Q3, not_3_out, not_4_out, not_5_out);
  and and_5 (and_5_out, not_2_out, not_3_out, Q1, Q0);
  and and_6 (and_6_out, not_2_out, Q2, Q1, not_5_out);
  and and_7 (and_7_out, A0, not_2_out, not_4_out, not_5_out);
  or or_2 (D2, and_5_out, and_6_out, and_7_out, and_9_out, and_8_out);
  and and_8 (and_8_out, A0, Q3, not_3_out, not_4_out, Q0);
  and and_9 (and_9_out, A0, not_2_out, Q2, not_4_out);
  and and_10 (and_10_out, not_1_out, not_2_out, not_3_out, not_4_out, Q0);
  and and_11 (and_11_out, not_1_out, not_2_out, Q2, Q1, Q0);
  and and_12 (and_12_out, not_1_out, not_2_out, not_3_out, Q1, not_5_out);
  and and_13 (and_13_out, not_1_out, Q3, not_3_out, not_4_out, not_5_out);
  and and_14 (and_14_out, A0, not_2_out, not_4_out, not_5_out);
  or or_3 (D1, and_10_out, and_12_out, and_11_out, and_13_out, and_14_out, and_15_out, and_16_out, and_17_out);
  and and_15 (and_15_out, A0, not_2_out, not_3_out, Q1, Q0);
  and and_16 (and_16_out, A0, not_2_out, Q2, not_4_out);
  and and_17 (and_17_out, A0, not_2_out, Q2, not_5_out);
  and and_18 (and_18_out, not_1_out, not_2_out, not_3_out, not_5_out);
  and and_19 (and_19_out, not_1_out, not_2_out, Q2, Q1, Q0);
  and and_20 (and_20_out, Q3, not_3_out, not_4_out, Q0);
  or or_4 (D0, and_18_out, and_19_out, and_20_out, and_21_out, and_22_out, and_23_out);
  and and_21 (and_21_out, A0, not_2_out, not_3_out, Q0);
  and and_22 (and_22_out, A0, not_2_out, Q2, Q1, not_5_out);
  and and_23 (and_23_out, A0, Q3, not_3_out, not_4_out);
  and and_24 (and_24_out, not_2_out, not_4_out, Q0);
  and and_25 (and_25_out, not_2_out, Q2, not_4_out);
  and and_26 (and_26_out, A0, not_2_out, not_4_out);
  or or_5 (A7, and_24_out, and_25_out, and_26_out, and_27_out);
  and and_27 (and_27_out, Q3, not_3_out, not_4_out, not_5_out);
  and and_28 (and_28_out, not_2_out, Q2, not_4_out);
  and and_29 (and_29_out, not_2_out, not_4_out, not_5_out);
  or or_6 (B7, and_29_out, and_28_out, and_30_out);
  and and_30 (and_30_out, Q3, not_3_out, not_4_out, Q0);
  and and_31 (and_31_out, not_2_out, not_4_out, not_5_out);
  and and_32 (and_32_out, not_2_out, Q2, not_4_out);
  or or_7 (C7, and_31_out, and_32_out, and_33_out);
  and and_33 (and_33_out, Q3, not_3_out, not_4_out, Q0);
  and and_34 (and_34_out, not_2_out, Q0);
  and and_35 (and_35_out, not_2_out, Q2);
  and and_36 (and_36_out, not_2_out, Q1);
  or or_8 (D7, and_34_out, and_36_out, and_35_out, and_37_out, and_38_out);
  and and_37 (and_37_out, A0, not_2_out);
  and and_38 (and_38_out, Q3, not_3_out, not_4_out, not_5_out);
  or or_9 (E7, not_2_out, and_39_out);
  and and_39 (and_39_out, not_3_out, not_4_out);
  and and_40 (and_40_out, not_3_out, not_4_out);
  or or_10 (F7, not_2_out, and_40_out);
  and and_41 (and_41_out, not_1_out, not_3_out, not_4_out);
  and and_42 (and_42_out, not_3_out, not_4_out, Q0);
  or or_11 (G7, and_41_out, and_42_out, and_43_out);
  and and_43 (and_43_out, Q3, not_3_out, not_4_out);

  // Notes on the sheet:
  //   AB'C'D'E + AB'C'DE' + AB'CDE + ABC'D'E'
  //   B'C'DE + B'CDE' + AB'D'E' + AB'CD' + ABC'D'E
  //   A'B'C'D'E + A'B'C'DE' + A'B'CDE + A'BC'D'E' + AB'D'E' + AB'C'DE + AB'CD' + AB'CE'
  //   A'B'C'E' + A'B'CDE + BC'D'E + AB'C'E + AB'CDE' + ABC'D'
  //   B’D’E + B’CD’ + AB’D’ + BC’D’E’
  //   B’D’E’ + B’CD’ + BC’D’E
  //   B’D’E’ + B’CD’ + BC’D’E
  //   B’E + B’D + B’C + AB’ + BC’D’E’
  //   B’ + C’D’
  //   B’ + C’D’
  //   A’C’D’ + C’D’E + BC’D’
endmodule

module mode_2_3_sub_circuit (
  input  A0,
  input  Q4,
  input  Q3,
  input  Q2,
  input  Q1,
  input  Q0,
  output D4,
  output D3,
  output D2,
  output D1,
  output D0,
  output A7,
  output B7,
  output C7,
  output D7,
  output E7,
  output F7,
  output G7
);

  wire and_1_out, and_2_out, and_3_out, and_4_out, and_5_out, and_6_out, and_7_out, and_8_out, and_9_out,
       and_10_out, and_11_out, and_12_out, and_13_out, and_14_out, and_15_out, and_16_out, and_17_out,
       and_18_out, and_19_out, and_20_out, and_21_out, and_22_out, and_23_out, and_24_out, and_25_out,
       and_26_out, and_27_out, and_28_out, and_29_out, and_30_out, and_31_out, and_32_out, and_33_out,
       and_34_out, and_35_out, and_36_out, and_37_out, and_38_out, and_39_out, and_40_out, and_41_out,
       and_42_out, and_43_out, and_44_out, and_45_out, and_46_out, and_47_out, and_48_out, and_49_out,
       and_50_out, and_51_out, and_52_out, and_53_out, and_54_out, and_55_out, and_56_out, and_57_out,
       and_58_out, and_59_out, and_60_out, and_61_out, and_62_out, and_63_out, and_64_out, and_65_out,
       and_66_out, and_67_out, and_68_out, and_69_out, and_70_out, and_71_out, and_72_out, and_73_out,
       and_74_out, and_75_out, and_76_out, and_77_out, and_78_out, and_79_out, not_1_out, not_2_out,
       not_3_out, not_4_out, not_5_out, not_6_out;

  not not_1 (not_1_out, A0);
  not not_2 (not_2_out, Q4);
  not not_3 (not_3_out, Q3);
  not not_4 (not_4_out, Q2);
  not not_5 (not_5_out, Q1);
  not not_6 (not_6_out, Q0);
  and and_1 (and_1_out, A0, Q4, not_3_out, not_4_out, not_5_out, not_6_out);
  and and_2 (and_2_out, A0, not_2_out, Q2, Q1);
  and and_3 (and_3_out, A0, not_2_out, Q2, Q0);
  or or_1 (D4, and_1_out, and_2_out, and_3_out, and_4_out);
  and and_4 (and_4_out, A0, not_2_out, not_3_out, Q2);
  and and_5 (and_5_out, not_1_out, not_2_out, Q2, Q1, Q0);
  and and_6 (and_6_out, not_1_out, not_2_out, not_3_out, Q2, Q1);
  and and_7 (and_7_out, not_1_out, not_2_out, Q3, not_4_out, not_5_out, not_6_out);
  and and_8 (and_8_out, not_1_out, Q4, not_3_out, not_4_out, not_5_out);
  and and_9 (and_9_out, A0, not_2_out, not_3_out, not_4_out);
  or or_2 (D3, and_6_out, and_5_out, and_7_out, and_8_out, and_9_out, and_10_out, and_11_out, and_12_out, and_13_out);
  and and_10 (and_10_out, A0, not_2_out, not_4_out, Q0);
  and and_11 (and_11_out, A0, not_2_out, not_4_out, Q1);
  and and_12 (and_12_out, A0, not_3_out, not_4_out, Q1);
  and and_13 (and_13_out, A0, not_2_out, Q3, Q2, not_5_out, not_6_out);
  and and_14 (and_14_out, not_2_out, not_3_out, not_4_out, Q1);
  and and_15 (and_15_out, not_2_out, not_4_out, Q1, Q0);
  and and_16 (and_16_out, not_1_out, not_2_out, Q2, not_5_out);
  and and_17 (and_17_out, not_1_out, not_2_out, Q3, Q2, not_6_out);
  and and_18 (and_18_out, not_2_out, Q3, Q2, not_5_out, not_6_out);
  or or_3 (D2, and_14_out, and_15_out, and_16_out, and_17_out, and_18_out, and_19_out, and_20_out, and_21_out);
  and and_19 (and_19_out, A0, not_2_out, not_3_out, not_4_out);
  and and_20 (and_20_out, A0, not_2_out, not_4_out, Q1);
  and and_21 (and_21_out, A0, not_3_out, not_4_out, Q1, Q0);
  and and_22 (and_22_out, not_1_out, not_2_out, not_3_out, not_5_out);
  and and_23 (and_23_out, not_1_out, not_2_out, not_4_out, not_5_out, not_6_out);
  and and_24 (and_24_out, not_1_out, not_2_out, Q2, not_5_out, Q0);
  and and_25 (and_25_out, not_1_out, not_2_out, Q3, Q1, not_6_out);
  and and_26 (and_26_out, not_1_out, Q4, not_3_out, not_4_out, Q0);
  and and_27 (and_27_out, A0, not_2_out, not_3_out, Q1);
  or or_4 (D1, and_22_out, and_23_out, and_24_out, and_25_out, and_26_out, and_27_out, and_28_out, and_29_out, and_30_out, and_31_out);
  and and_28 (and_28_out, A0, not_2_out, Q1, Q0);
  and and_29 (and_29_out, A0, not_2_out, Q3, not_4_out, Q0);
  and and_30 (and_30_out, A0, not_2_out, Q3, Q2, not_5_out, not_6_out);
  and and_31 (and_31_out, A0, Q4, not_3_out, not_4_out, not_6_out);
  and and_32 (and_32_out, not_3_out, not_4_out, not_5_out, not_6_out);
  and and_33 (and_33_out, not_2_out, not_4_out, not_5_out, Q0);
  and and_34 (and_34_out, not_2_out, not_3_out, Q0);
  and and_35 (and_35_out, not_2_out, Q3, Q2, not_6_out);
  or or_5 (D0, and_32_out, and_34_out, and_33_out, and_35_out, and_36_out, and_37_out, and_38_out);
  and and_36 (and_36_out, Q4, not_3_out, not_4_out, not_6_out);
  and and_37 (and_37_out, A0, not_2_out, not_4_out, not_5_out);
  and and_38 (and_38_out, A0, not_3_out, not_4_out, not_5_out);
  and and_39 (and_39_out, not_2_out, not_4_out, not_5_out);
  and and_40 (and_40_out, not_2_out, not_3_out, Q1, Q0);
  and and_41 (and_41_out, not_2_out, Q3, not_4_out, not_6_out);
  and and_42 (and_42_out, not_2_out, not_3_out, Q2, not_6_out);
  or or_6 (A7, and_39_out, and_40_out, and_42_out, and_41_out, and_43_out, and_44_out, and_45_out);
  and and_43 (and_43_out, not_2_out, Q3, not_5_out);
  and and_44 (and_44_out, not_2_out, Q3, Q2, Q0);
  and and_45 (and_45_out, Q4, not_3_out, not_4_out);
  and and_46 (and_46_out, not_2_out, not_4_out);
  and and_47 (and_47_out, not_2_out, not_5_out);
  and and_48 (and_48_out, not_3_out, not_4_out, Q0);
  or or_7 (B7, and_46_out, and_47_out, and_48_out, and_49_out, and_50_out);
  and and_49 (and_49_out, not_3_out, not_4_out, Q1);
  and and_50 (and_50_out, not_2_out, Q3, not_6_out);
  and and_51 (and_51_out, not_2_out, not_3_out, not_5_out);
  and and_52 (and_52_out, not_2_out, not_3_out, not_6_out);
  and and_53 (and_53_out, not_2_out, not_5_out, Q0);
  and and_54 (and_54_out, not_2_out, Q2, Q1);
  or or_8 (C7, and_51_out, and_52_out, and_53_out, and_54_out, and_55_out, and_56_out);
  and and_55 (and_55_out, not_2_out, Q3, not_4_out);
  and and_56 (and_56_out, Q4, not_3_out, not_4_out);
  and and_57 (and_57_out, not_2_out, not_3_out, not_4_out, not_5_out);
  and and_58 (and_58_out, not_2_out, not_3_out, Q2, not_6_out);
  and and_59 (and_59_out, not_2_out, not_3_out, Q1, Q0);
  and and_60 (and_60_out, not_2_out, Q2, not_5_out, not_6_out);
  or or_9 (D7, and_57_out, and_59_out, and_58_out, and_60_out, and_61_out, and_62_out, and_63_out);
  and and_61 (and_61_out, not_2_out, Q3, not_5_out, Q0);
  and and_62 (and_62_out, not_2_out, Q3, Q2, Q0);
  and and_63 (and_63_out, Q4, not_3_out, not_4_out, not_6_out);
  and and_64 (and_64_out, not_3_out, not_4_out, not_5_out, not_6_out);
  and and_65 (and_65_out, not_2_out, not_4_out, not_5_out, Q0);
  and and_66 (and_66_out, not_2_out, not_3_out, Q1, Q0);
  or or_10 (E7, and_64_out, and_65_out, and_66_out, and_67_out, and_68_out);
  and and_67 (and_67_out, not_2_out, Q3, Q2, not_5_out, not_6_out);
  and and_68 (and_68_out, Q4, not_3_out, not_4_out, not_6_out);
  and and_69 (and_69_out, not_3_out, not_4_out, not_5_out, not_6_out);
  and and_70 (and_70_out, not_2_out, not_3_out, not_5_out, Q0);
  and and_71 (and_71_out, not_2_out, not_4_out, not_5_out, Q0);
  and and_72 (and_72_out, not_2_out, Q2, Q1);
  or or_11 (F7, and_69_out, and_70_out, and_71_out, and_72_out, and_73_out, and_74_out);
  and and_73 (and_73_out, not_2_out, Q3, Q1, not_6_out);
  and and_74 (and_74_out, Q4, not_3_out, not_4_out, Q1);
  and and_75 (and_75_out, not_3_out, not_4_out, Q1, Q0);
  and and_76 (and_76_out, not_2_out, Q2);
  and and_77 (and_77_out, not_2_out, Q3, not_5_out, Q0);
  and and_78 (and_78_out, not_2_out, Q3, Q1, not_6_out);
  or or_12 (G7, and_75_out, and_76_out, and_77_out, and_78_out, and_79_out);
  and and_79 (and_79_out, Q4, not_3_out, not_4_out, not_6_out);

  // Notes on the sheet:
  //   AB’C’D + AB’DF + AB’DE + ABC’D’E’F’
  //   AB'C'D' + AB'D'F + AB'D'E + AC'D'E + A'B'C'DE + A'B'DEF + A'BC'D'E' + A'B'CD'E'F' + AB'CDE'F'
  //   B'C'D'E + B'D'EF + A'B'DE' + AB'C'D' + AB'D'E + A'B'CDF' + B'CDE'F' + AC'D'EF
  //   A'B'C'E' + AB'C'E + AB'EF + A'B'D'E'F' + A'B'DE'F + A'B'CEF' + A'BC'D'F + AB'CD'F + ABC'D'F' + AB'CDE'F'
  //   C'D'E'F' + B'C'F + B'D'E'F + B'CDF' + BC'D'F' + AB'D'E' + AC'D'E'
  //   B'D'E' + B'C'EF + B'C'DF' + B'CD'F' + B'CE' + B'CDF + BC'D'
  //   B'D' + B'E' + C'D'F + C'D'E + B'CF'
  //   B’C’E’ + B’C’F’ + B’E’F + B’DE + B’CD’ + BC’D’
  //   B’C’D’E’ + B’C’EF + B’C’DF’ + B’DE’F’ + B’CE’F + B’CDF + BC’D’F’
  //   C’D’E’F’ + B’D’E’F + B’C’EF + B’CDE’F’ + BC’D’F’
  //   B'DE + C'D'E'F' + B'C'E'F + B'D'E'F + B'CEF' + BC'D'E
  //   B'D + C'D'EF + B'CE'F + B'CEF' + BC'D'F'
endmodule
